# Fritzing sketch 17010011005 (saved by Fritzing 0.9.3b)
breadboards: 2

parts:
  Parça1 = Arduino Mega 2560 (Rev3)
  Nokia_5110_LCD_Module1 = Nokia 5110 LCD
  R1 = Resistor [tolerance=±5% resistance=330 package="2010 [SMD]"]
  Part1 = KY-015 Temperature & Humidity Sensor Module [package="Breakout board"]
  S1 = Pushbutton [package="[SMD]"]
  R2 = Resistor [tolerance=±5% resistance=10k package="2010 [SMD]"]
  R4 = Resistor [tolerance=±5% resistance=10k package="2010 [SMD]"]
  Parça2 = Barometric Pressure Sensor - BMP180 Breakout (GY-68)  # not connected
  R5 = Resistor [tolerance=±5% resistance=330 package="2010 [SMD]"]
  R6 = Resistor [tolerance=±5% resistance=330 package="2010 [SMD]"]
  R7 = Resistor [tolerance=±5% resistance=330 package="2010 [SMD]"]
  U1 = ESP8266 WiFi Module [part_number=ESP8266]
  R3 = Photocell (LDR) [package=THT]
  LED1 = RGB LED - (4 legs) [package="5 mm [THT]"]
  Water_Level_Sensor1 = Water Level Sensor

nets:
  N1: Parça1.A0, R4.Pin_1, R3.pin_0
  N2: Parça1.A1, Water_Level_Sensor1.SIG
  N3: Parça1.D19/RX1, U1.TXD
  N4: Parça1.D18/TX1, U1.RXD
  N5: Parça1.D13_PWM, R1.Pin_0
  N6: Parça1.D12_PWM, Nokia_5110_LCD_Module1.CE
  N7: Parça1.D11_PWM, Nokia_5110_LCD_Module1.RST
  N8: Parça1.D10_PWM, Nokia_5110_LCD_Module1.D/C
  N9: Parça1.D9_PWM, Nokia_5110_LCD_Module1.Din
  N10: Parça1.D8_PWM, Nokia_5110_LCD_Module1.CLK
  VCC: Parça1.3V3, Nokia_5110_LCD_Module1.VCC, U1.VCC, U1.CH_PD
  5V: Parça1.5V, Part1.Vin, S1.Pin_3, S1.Pin_4, R3.pin_1, LED1.common_anode, Water_Level_Sensor1.VCC
  GND: Parça1.GND, Nokia_5110_LCD_Module1.GND, Part1.-, R2.Pin_1, R4.Pin_0, U1.GND, Water_Level_Sensor1.GND
  N11: Parça1.D2_PWM, S1.Pin_1, S1.Pin_2, R2.Pin_0
  N12: Parça1.D4_PWM, R7.Pin_0
  N13: Parça1.D5_PWM, R5.Pin_0
  N14: Parça1.D6_PWM, R6.Pin_0
  N15: Parça1.D7_PWM, Part1.S
  N16: Nokia_5110_LCD_Module1.BL, R1.Pin_1
  N17: R5.Pin_1, LED1.green_cathode
  N18: R6.Pin_1, LED1.blue_cathode
  N19: R7.Pin_1, LED1.red_cathode

custom parts:
  Nokia 5110 LCD: Nokia 5110 Graphic 84*48 LCD module <Blue Version>
  KY-015 Temperature & Humidity Sensor Module: KY-015 temperature and humidity sensor module, provides a low-latency serial interface to measure humidity and temperature.
  ESP8266 WiFi Module: Generic WiFi Module based on the ESP8266 with onboard PCB antenna and UART communications
  Water Level Sensor: A water level sensor. This sensor operates at 3V to 5V. The Sig (signal) pin outputs an analogue signal that is in proportion to the amount of water in contact with the sensor.
